# Fritzing sketch desk-droid (saved by Fritzing 0.9.6b)
breadboards: 1

parts:
  A1 = ESP32-S3 supermini
  OLED_I2C1 = OLED 128x64 I2C Monochrome Display
  SG1 = Buzzer 12mm [part_number=COM-07950 package=buzzer-12mm-ns]
  Sensor1 = TTP223B Capacitive Touch Sensor Module
  TEMT6000_Breakout_Board1 = TEMT6000 Breakout Board [part_number=TEMT6000]
  Part2 = Adafruit ADXL345 [part_number="Adafruit #1231"]

nets:
  N1: A1.Pin_10, Part2.SDA/SDIO
  N2: A1.Pin_11, Part2.SCL
  N3: A1.Pin_32, TEMT6000_Breakout_Board1.SIG
  N4: A1.Pin_34, Sensor1.SIG
  N5: A1.Pin_35, SG1.1
  N6: A1.Pin_36, OLED_I2C1.SDA
  N7: A1.Pin_37, OLED_I2C1.SCK
  VCC: A1.Pin_38, OLED_I2C1.VDD, Sensor1.VCC, TEMT6000_Breakout_Board1.VCC, Part2.VIN
  GND: A1.Pin_39, OLED_I2C1.GND, SG1.2, Sensor1.GND, TEMT6000_Breakout_Board1.GND, Part2.GND

custom parts:
  ESP32-S3 supermini: Esp32-S3 Development board ESP32 SuperMini development board ESP32 Development board WiFi Bluetooth.
  Buzzer 12mm: Buzzer 12mm Spark Fun Electronics SKU : Comp-Buzzer Through hole This is a small 12mm round speaker that operates around the audible 2kHz range. You can use these speakers to create simple music or user interfaces. This is not a true piezoelectric speaker but behaves similarly. Instead of a piezoelectric crystal that vibrates with an electric current, this tiny speaker uses an electromagnet to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
  TTP223B Capacitive Touch Sensor Module: The TTP223B capacitive touch sensor module uses the TTP223B IC. The appropriate voltage is approximately 2 to 5.5 volts.
  TEMT6000 Breakout Board: The TEMT6000 is an ambient light sensor produced by Vishay Semiconductors. The sensor operates at both 3V3 and 5V and has analog output (with higher output voltage meaning more light) from the SIG pin.
  Adafruit ADXL345: Filling out our accelerometer offerings, we now have the really lovely digital ADXL345 from Analog Devices, a triple-axis accelerometer with digital I2C and SPI interface breakout. We added an on-board 3.3V regulator and logic-level shifting circuitry, making it a perfect choice for interfacing with any 3V or 5V microcontroller such as the Arduino. The sensor has three axes of measurements, X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
